// Logisim project CS251_Branches.circ as structural Verilog: 1 circuit, main circuit main
module main (
  input  [4:0] Flags,
  input  [3:0] d,
  output Branch
);

  wire BG, BGE, BL, BLE, BNC, BNS, BNV, BNZ, BUG, BULE, not_3_out;

  not not_1 (BNS, Flags[0]);
  xor xor_1 (BL, Flags[0], Flags[2]);
  not not_2 (BNZ, Flags[1]);
  not not_3 (not_3_out, Flags[3]);
  not not_4 (BNC, Flags[3]);
  not not_5 (BNV, Flags[2]);
  not not_6 (BGE, BL);
  or or_1 (BLE, BL, Flags[1]);
  or or_2 (BULE, Flags[1], not_3_out);
  not not_7 (BG, BLE);
  not not_8 (BUG, BULE);
  Multiplexer #(.select(4)) multiplexer_1 (
    .in0(1'b1), .in2(BL), .in3(BGE), .in4(BLE), .in5(BG), .in6(BULE), .in7(BUG), .in8(Flags[1]), .in9(BNZ),
    .in10(Flags[3]), .in11(BNC), .in12(Flags[0]), .in13(BNS), .in14(Flags[2]), .in15(BNV), .out(Branch),
    .sel(d));  // open: in1

  // Other names for the same wires on the sheet: BS = Flags[0]; s = Flags[0]; BZ = Flags[1]; z = Flags[1];
  //   BV = Flags[2]; v = Flags[2]; BC = Flags[3]; c = Flags[3]; cb = Flags[4]
endmodule
