// Logisim project CS251_MainHERA.circ as structural Verilog: 6 circuits, main circuit PC
module main (
  input  reset
);

  wire branch, button_one_out, button_two, CaRt, Check, clk, comparator_1_eq, comparator_2_eq, ifStore, LOAD,
       multiplexer_3_out, STORE, two_c, valueOfB1, valueOfStore, xor_1_out;
  wire [3:0] a, b, d;
  wire [4:0] alsu_1_f_out, Flags_final, Flags_out;
  wire [15:0] ALSU_out, bit_extender_1_out, bit_extender_2_out, FP, jump, multiplexer_1_out,
       multiplexer_2_out, PC_out, PC_out_new, R1, R2, R3, R12, R13, RAM_out, Rb, Rb_in, Rd, Rd_out,
       registerbank_1_ra_out;
  wire [15:12] Instruction;
  wire [63:48] rg2;

  Clock clock_1 (.out(clk));
  xor xor_1 (xor_1_out, CaRt, branch);
  Button u_button_two (.out(button_two));
  Hex_Digit_Display #(.decimalPoint("false")) hex_digit_display_1 (.value(R12[15:12]));
  assign bit_extender_1_out = {{15{1'b0}}, valueOfB1};  // Bit_Extender bit_extender_1
  Multiplexer #(.width(16)) multiplexer_1 (.in0(Rd), .in1(bit_extender_1_out), .out(multiplexer_1_out), .sel(Check));
  Hex_Digit_Display #(.decimalPoint("false")) hex_digit_display_2 (.value(R12[11:8]));
  Hex_Digit_Display #(.decimalPoint("false")) hex_digit_display_3 (.value(R12[7:4]));
  Multiplexer #(.width(16)) multiplexer_2 (
    .in0(multiplexer_1_out), .in1(bit_extender_2_out), .out(multiplexer_2_out), .sel(two_c));
  assign bit_extender_2_out = {{15{1'b0}}, button_two};  // Bit_Extender bit_extender_2
  Hex_Digit_Display #(.decimalPoint("false")) hex_digit_display_4 (.value(R1[15:12]));
  Hex_Digit_Display #(.decimalPoint("false")) hex_digit_display_5 (.value(R1[11:8]));
  Hex_Digit_Display #(.decimalPoint("false")) hex_digit_display_6 (.value(R12[3:0]));
  Hex_Digit_Display #(.decimalPoint("false")) hex_digit_display_7 (.value(R13[15:12]));
  Hex_Digit_Display #(.decimalPoint("false")) hex_digit_display_8 (.value(R1[7:4]));
  Hex_Digit_Display #(.decimalPoint("false")) hex_digit_display_9 (.value(R1[3:0]));
  Hex_Digit_Display #(.decimalPoint("false")) hex_digit_display_10 (.value(R13[11:8]));
  Hex_Digit_Display #(.decimalPoint("false")) hex_digit_display_11 (.value(R13[7:4]));
  Multiplexer multiplexer_3 (.in0(STORE), .out(multiplexer_3_out), .sel(valueOfStore));  // open: in1
  PC pc_1 (
    .reset(reset), .branch(xor_1_out), .branch_address(jump), .CLK(clk), .PC_out(PC_out),
    .instruction({Instruction, d, a, b}));
  Hex_Digit_Display #(.decimalPoint("false")) hex_digit_display_12 (.value(R2[15:12]));
  Hex_Digit_Display #(.decimalPoint("false")) hex_digit_display_13 (.value(R2[11:8]));
  LED Cb (.in(Flags_final[4]));
  LED C (.in(Flags_final[3]));
  Hex_Digit_Display #(.decimalPoint("false")) hex_digit_display_14 (.value(R13[3:0]));
  control_unit control_unit_1 (
    .instruction({Instruction, d, a, b}), .flags_out(Flags_out), .Rb(Rb), .PC_out(PC_out), .jump_to(jump),
    .branch(branch), .load(LOAD), .store(STORE), .CaRt(CaRt), .Rb_in(Rb_in));
  Hex_Digit_Display #(.decimalPoint("false")) hex_digit_display_15 (.value(PC_out[15:12]));
  Hex_Digit_Display #(.decimalPoint("false")) hex_digit_display_16 (.value(PC_out[11:8]));
  Hex_Digit_Display #(.decimalPoint("false")) hex_digit_display_17 (.value(R2[7:4]));
  Hex_Digit_Display #(.decimalPoint("false")) hex_digit_display_18 (.value(R2[3:0]));
  LED V (.in(Flags_final[2]));
  LED Z (.in(Flags_final[1]));
  LED S (.in(Flags_final[0]));
  Hex_Digit_Display #(.decimalPoint("false")) hex_digit_display_19 (.value(FP[15:12]));
  Hex_Digit_Display #(.decimalPoint("false")) hex_digit_display_20 (.value(PC_out[7:4]));
  Hex_Digit_Display #(.decimalPoint("false")) hex_digit_display_21 (.value(PC_out[3:0]));
  Hex_Digit_Display #(.decimalPoint("false")) hex_digit_display_22 (.value(R3[15:12]));
  Hex_Digit_Display #(.decimalPoint("false")) hex_digit_display_23 (.value(FP[11:8]));
  Hex_Digit_Display #(.decimalPoint("false")) hex_digit_display_24 (.value(FP[7:4]));
  Hex_Digit_Display #(.decimalPoint("false")) hex_digit_display_25 (.value(R3[11:8]));
  Hex_Digit_Display #(.decimalPoint("false")) hex_digit_display_26 (.value(R3[7:4]));
  Hex_Digit_Display #(.decimalPoint("false")) hex_digit_display_27 (.value(FP[3:0]));
  RegisterBank registerbank_1 (
    .reset(reset), .ins_two_c(two_c), .Rd_in(multiplexer_2_out), .Clock(clk), .STORE(multiplexer_3_out),
    .Instruction({Instruction, d, a, b}), .PC_in(PC_out), .Ra_out(registerbank_1_ra_out), .Rb_out(Rb),
    .PC_out(PC_out_new), .Rd_out(Rd_out), .Rg_1({R3, R2, R1}), .Rg_2({rg2, FP, R13, R12}));
  Hex_Digit_Display #(.decimalPoint("false")) hex_digit_display_28 (.value(R3[3:0]));
  Hex_Digit_Display #(.decimalPoint("false")) hex_digit_display_29 (.value(rg2[63:60]));
  Hex_Digit_Display #(.decimalPoint("false")) hex_digit_display_30 (.value(rg2[59:56]));
  Hex_Digit_Display #(.decimalPoint("false")) hex_digit_display_31 (.value(Instruction));
  Hex_Digit_Display #(.decimalPoint("false")) hex_digit_display_32 (.value(d));
  Hex_Digit_Display #(.decimalPoint("false")) hex_digit_display_33 (.value(rg2[55:52]));
  Hex_Digit_Display #(.decimalPoint("false")) hex_digit_display_34 (.value(rg2[51:48]));
  Hex_Digit_Display #(.decimalPoint("false")) hex_digit_display_35 (.value(a));
  Hex_Digit_Display #(.decimalPoint("false")) hex_digit_display_36 (.value(b));
  dataMem datamem_1 (
    .Rd_out(Rd_out), .Rb(Rb), .a(a), .opcode(Instruction), .CLK(clk), .flags_in(Flags_out),
    .checkStore(ifStore), .RAM_out(RAM_out), .flags_out(Flags_final));
  Button button_one (.out(button_one_out));
  Comparator #(.width(16)) comparator_1 (.a(16'hfff0), .b(Rb), .eq(comparator_1_eq));  // open: gt, lt
  Comparator #(.width(16)) comparator_2 (.a(16'hfff0), .b(Rd_out), .eq(comparator_2_eq));  // open: gt, lt
  ALSU alsu_1 (
    .flags_in(Flags_out), .Ra(registerbank_1_ra_out), .Rb(Rb), .Rd(Rd_out),
    .instruction({Instruction, d, a, b}), .result(ALSU_out), .f_out(alsu_1_f_out));
  and and_1 (two_c, ~d[0], ~d[1], d[2], d[3], ~Instruction[12], Instruction[13], ~Instruction[14], ~Instruction[15]);  // AND_Gate
  and and_2 (valueOfB1, comparator_1_eq, ~ifStore, button_one_out);  // AND_Gate
  Multiplexer #(.width(16)) multiplexer_4 (.in0(ALSU_out), .in1(RAM_out), .out(Rd), .sel(LOAD));
  and and_3 (valueOfStore, ifStore, comparator_2_eq);
  Comparator #(.width(16)) comparator_3 (.a(16'hfff0), .b(Rb), .eq(Check));  // open: gt, lt
  FlagBank flagbank_1 (.r(reset), .flagsIn(alsu_1_f_out), .Clock(clk), .flagsOut(Flags_out));

  // Other names for the same wires on the sheet: Instruction[11:0] = {d, a, b}; op[3:0] = Instruction;
  //   rg1[47:0] = {R3, R2, R1}; rg2[47:0] = {FP, R13, R12}; SP[15:0] = rg2

  // Notes on the sheet:
  //   hit reset here so we don't have to reload RAM
  //   Checking if the button 1 and load instruction are both on
  //   If we are jumping to a different instruction (via branch, or call/return),
  //   find the location of that instruction. Also control load/store
  //   Ignoring STORE for the case of button1
  //   Checking if button two is pressed along with the appropriate instruction to increment the counter
  //   (1) Begin by using the PC to read the correct instruction from memory (via ROM)
  //   (2) We need to find the values of Rd, Ra, and Rb.
  //   So, we go through the register bank...
  //   If we are calling LOAD/STORE...
  //   (3) Now that we have the operation & registers,
  //   we can perform the arithmetic.
  //   Now, depending on the operation, we need to set Rd
  //   (4) Update the flags after the arithmetic
  //   Checking if Rb is equal to 0xfff0 for purposes of LOAD
  //   Checking if the opcode is getting 2C for button 2
  //   Checking if button is pressed
endmodule

module PC (
  input  reset,
  input  branch,
  input  [15:0] branch_address,
  input  CLK,
  output [15:0] PC_out,
  output [15:0] instruction
);

  wire not_1_out;

  not not_1 (not_1_out, branch);
  Counter #(.max('hffff), .width(16)) counter_1 (
    .clr(reset), .load(branch), .count(not_1_out), .clk(CLK), .D(branch_address), .Q(PC_out));  // open: up, carry
  ROM #(.addrWidth(16), .dataWidth(16)) rom_1 (.addr(PC_out), .data(instruction));

  // Other names for the same wires on the sheet: B_Add[15:0] = branch_address

  // Notes on the sheet:
  //   contents of rom_1 (hex, n*v repeats v):
  //   e600 e707 e300 f3ff e8f0 f8ff 4b08 3068 b0b0 eb0d fb00 180b 3180 2cc0 3068 b0c0 eb14 fb00 180b 3280
  //   3680 8667 3380 eb04 fb00 190b
endmodule

module FlagBank (
  input  r,
  input  [4:0] flagsIn,
  input  Clock,
  output [4:0] flagsOut
);

  D_Flip_Flop sign (.clk(Clock), .D(flagsIn[0]), .Q(flagsOut[0]), .reset(r));  // open: Qn, preset
  D_Flip_Flop zero (.clk(Clock), .D(flagsIn[1]), .Q(flagsOut[1]), .reset(r));  // open: Qn, preset
  D_Flip_Flop overflow (.clk(Clock), .D(flagsIn[2]), .Q(flagsOut[2]), .reset(r));  // open: Qn, preset
  D_Flip_Flop carry (.clk(Clock), .D(flagsIn[3]), .Q(flagsOut[3]), .reset(r));  // open: Qn, preset
  D_Flip_Flop carry_block (.clk(Clock), .D(flagsIn[4]), .Q(flagsOut[4]), .reset(r));  // open: Qn, preset
endmodule

module Branching (
  input  [4:0] Flags,
  input  [3:0] d,
  output Branch
);

  wire BG, BGE, BL, BLE, BNC, BNS, BNV, BNZ, BUG, BULE, not_3_out;

  not not_1 (BNS, Flags[0]);
  xor xor_1 (BL, Flags[0], Flags[2]);
  not not_2 (BNZ, Flags[1]);
  not not_3 (not_3_out, Flags[3]);
  not not_4 (BNC, Flags[3]);
  not not_5 (BNV, Flags[2]);
  not not_6 (BGE, BL);
  or or_1 (BLE, BL, Flags[1]);
  or or_2 (BULE, Flags[1], not_3_out);
  not not_7 (BG, BLE);
  not not_8 (BUG, BULE);
  Multiplexer #(.select(4)) multiplexer_1 (
    .in0(1'b1), .in1(1'b1), .in2(BL), .in3(BGE), .in4(BLE), .in5(BG), .in6(BULE), .in7(BUG), .in8(Flags[1]),
    .in9(BNZ), .in10(Flags[3]), .in11(BNC), .in12(Flags[0]), .in13(BNS), .in14(Flags[2]), .in15(BNV),
    .out(Branch), .sel(d));

  // Other names for the same wires on the sheet: BS = Flags[0]; s = Flags[0]; BZ = Flags[1]; z = Flags[1];
  //   BV = Flags[2]; v = Flags[2]; BC = Flags[3]; c = Flags[3]; cb = Flags[4]
endmodule

module dataMem (
  input  [15:0] Rd_out,
  input  [15:0] Rb,
  input  [3:0] a,
  input  [3:0] opcode,
  input  CLK,
  input  [4:0] flags_in,
  output checkStore,
  output [15:0] RAM_out,
  output [4:0] flags_out
);

  wire comparator_1_eq, comparator_1_lt, LD;
  wire [1:0] and_4_out;
  wire [15:0] adder_1_out, bit_extender_1_out;

  and and_1 (LD, ~opcode[1], opcode[2], ~opcode[3]);  // AND_Gate
  and and_2 (checkStore, opcode[1], opcode[2], ~opcode[3]);  // AND_Gate
  Adder #(.width(16)) adder_1 (.a(Rb), .b(bit_extender_1_out), .out(adder_1_out));  // open: cin, cout
  assign bit_extender_1_out = {{11{1'b0}}, {opcode[0], a}};  // Bit_Extender bit_extender_1
  RAM #(.addrWidth(16), .asyncread("true"), .dataWidth(16)) theRAM (
    .addr(adder_1_out), .we(checkStore), .oe(LD), .clk(CLK), .din(Rd_out), .dout(RAM_out));
  Comparator #(.width(16)) comparator_1 (
    .a(RAM_out), .b({16{1'b0}}), .eq(comparator_1_eq), .lt(comparator_1_lt));  // open: gt
  and and_3 (and_4_out[1], comparator_1_eq, LD);
  and and_4 (and_4_out[0], comparator_1_lt, LD);
  Multiplexer #(.width(2)) multiplexer_1 (.in0(flags_in[1:0]), .in1(and_4_out), .out(flags_out[1:0]), .sel(LD));

  assign flags_out[4:2] = flags_in[4:2];

  // Other names for the same wires on the sheet: b12 = opcode[0]; ST = checkStore; sz_in[1:0] = flags_in[1:0];
  //   sz_out[1:0] = flags_out[1:0]

  // Notes on the sheet:
  //   opcode controls load/store
endmodule

module control_unit (
  input  [15:0] instruction,
  input  [4:0] flags_out,
  input  [15:0] Rb,
  input  [15:0] PC_out,
  output [15:0] jump_to,
  output branch,
  output load,
  output store,
  output CaRt,
  output [15:0] Rb_in
);

  wire and_1_out, and_5_out, and_6_out, and_7_out, and_8_out, BJDreset, branch_out, or_1_out, xor_1_out;
  wire [15:0] adder_2_out, bit_extender_1_out, bit_extender_2_out, multiplexer_1_out;

  and and_1 (and_1_out, ~instruction[13], ~instruction[14], ~instruction[15]);  // AND_Gate
  and and_2 (branch, branch_out, and_1_out);
  and and_3 (load, ~instruction[13], instruction[14], ~instruction[15]);  // AND_Gate
  and and_4 (store, instruction[13], instruction[14], ~instruction[15]);  // AND_Gate
  and and_5 (and_5_out, ~instruction[15], ~instruction[14], instruction[13], ~instruction[12]);  // AND_Gate
  Branching branching_1 (.Flags(flags_out), .d(instruction[11:8]), .Branch(branch_out));
  and and_6 (and_6_out, ~instruction[8], ~instruction[9], ~instruction[10], ~instruction[11]);  // AND_Gate
  and and_7 (and_7_out, instruction[8], ~instruction[9], ~instruction[10], ~instruction[11]);  // AND_Gate
  and and_8 (and_8_out, ~instruction[12], instruction[13], ~instruction[14], ~instruction[15]);  // AND_Gate
  assign bit_extender_1_out = {{15{and_5_out}}, and_5_out};  // Bit_Extender bit_extender_1
  or or_1 (or_1_out, and_6_out, and_7_out);
  Adder #(.width(16)) adder_1 (.a(bit_extender_1_out), .b(PC_out), .out(Rb_in));  // open: cin, cout
  and and_9 (CaRt, or_1_out, and_8_out);
  assign bit_extender_2_out = {{8{instruction[3]}}, {instruction[3:0], instruction[7:4]}};  // Bit_Extender bit_extender_2
  Adder #(.width(16)) adder_2 (.a(PC_out), .b(bit_extender_2_out), .out(adder_2_out));  // open: cin, cout
  Multiplexer #(.width(16)) multiplexer_1 (.in0(Rb), .in1({16{1'b0}}), .out(multiplexer_1_out), .sel(BJDreset));
  Multiplexer #(.width(16)) multiplexer_2 (.in0(adder_2_out), .in1(multiplexer_1_out), .out(jump_to), .sel(xor_1_out));
  xor xor_1 (xor_1_out, instruction[12], CaRt);
  and and_10 (BJDreset, instruction[8], ~instruction[9], ~instruction[10], ~instruction[11]);  // AND_Gate

  // Other names for the same wires on the sheet: b[3:0] = instruction[7:4]; a[3:0] = instruction[3:0];
  //   d[3:0] = instruction[11:8]; o4 = instruction[12]; op[3:0] = instruction[15:12]

  // Notes on the sheet:
  //    Check to see if we need to branch/jump
  //   Using the opcode for specific instructions
  //   put this into reg bank
  //   register branching
  //   offset
  //   If register branching, jump to Rb
  //   Otherwise, relative branching: jump to PC + offest
  //   If we are branching, where are we going?
  //   Same logic as in the register bank to handle the CaRt flag 
  //   CALL: Call func at Rb, new stack frame at Ra
  //   R12 is the new value of the FP, R13 is the branch address
  //   RETURN: jump/return if return address in Rb & caller's FP in Ra
endmodule
