// Logisim project CS251_RegisterBank.circ as structural Verilog: 4 circuits, main circuit RegisterBank
module RegisterBank (
  input  reset,
  input  ins_two_c,
  input  [15:0] Rd_in,
  input  Clock,
  input  STORE,
  input  [15:0] Instruction,
  input  [15:0] PC_in,
  output [15:0] Ra_out,
  output [15:0] Rb_out,
  output [15:0] PC_out,
  output [15:0] Rd_out,
  output [47:0] Rg_1,
  output [63:0] Rg_2
);

  wire and_1_out, and_2_out, and_3_out, and_4_out, and_5_out, and_6_out, and_7_out, and_8_out, and_9_out,
       and_10_out, and_11_out, and_12_out, and_13_out, and_14_out, and_15_out, enR1, enR2, enR3, enR4, enR5,
       enR6, enR7, enR8, enR9, enR10, enR11, enR12, enR13, enR14, enR15;
  wire [3:0] d;
  wire [15:0] adder_1_out, R0, R4, R5, R6, R7, R8, R9, R10, R11, toR0, toR1, toR2, toR3, toR4, toR5, toR6,
       toR7, toR8, toR9, toR10, toR11, toR12, toR13, toR14, toR15;

  RegEnable regenable_1 (
    .opcode(Instruction[15:12]), .Rd(d), .Ra(Instruction[7:4]), .Rb(Instruction[3:0]), .R1(enR1), .R2(enR2),
    .R3(enR3), .R4(enR4), .R5(enR5), .R6(enR6), .R7(enR7), .R8(enR8), .R9(enR9), .R10(enR10), .R11(enR11),
    .R12(enR12), .R13(enR13), .R14(enR14), .R15(enR15));
  Multiplexer #(.width(4)) multiplexer_1 (.in0(Instruction[11:8]), .in1(Instruction[7:4]), .out(d), .sel(ins_two_c));
  Adder #(.width(16)) adder_1 (.a(PC_in), .b(16'h1), .out(adder_1_out));  // open: cin, cout
  and and_1 (and_1_out, enR1, ~STORE);  // AND_Gate
  and and_2 (and_2_out, enR2, ~STORE);  // AND_Gate
  and and_3 (and_3_out, enR3, ~STORE);  // AND_Gate
  and and_4 (and_4_out, enR4, ~STORE);  // AND_Gate
  and and_5 (and_5_out, enR5, ~STORE);  // AND_Gate
  and and_6 (and_6_out, enR6, ~STORE);  // AND_Gate
  and and_7 (and_7_out, enR7, ~STORE);  // AND_Gate
  RegSelect regselect_1 (
    .Instruction(Instruction), .Rd(Rd_in), .New_PC(adder_1_out), .Old_FP(Rg_2[47:32]), .R1(toR1),
    .out_6(toR2), .out_7(toR3), .out_8(toR4), .out_9(toR5), .out_10(toR6), .out_11(toR7), .out_12(toR8),
    .out_13(toR9), .out_14(toR10), .out_15(toR11), .out_16(toR12), .out_17(toR13), .out_18(toR14),
    .out_19(toR15));
  Register #(.width(16)) register_1 (.D(toR0), .en(1'b0), .clk(Clock), .Q(R0));  // open: clr
  Register #(.width(16)) register_2 (.D(toR1), .en(and_1_out), .clk(Clock), .Q(Rg_1[15:0]), .clr(reset));
  Register #(.width(16)) register_3 (.D(toR2), .en(and_2_out), .clk(Clock), .Q(Rg_1[31:16]), .clr(reset));
  Register #(.width(16)) register_4 (.D(toR3), .en(and_3_out), .clk(Clock), .Q(Rg_1[47:32]), .clr(reset));
  Register #(.width(16)) register_5 (.D(toR4), .en(and_4_out), .clk(Clock), .Q(R4), .clr(reset));
  Register #(.width(16)) register_6 (.D(toR5), .en(and_5_out), .clk(Clock), .Q(R5), .clr(reset));
  Register #(.width(16)) register_7 (.D(toR6), .en(and_6_out), .clk(Clock), .Q(R6), .clr(reset));
  Register #(.width(16)) register_8 (.D(toR7), .en(and_7_out), .clk(Clock), .Q(R7), .clr(reset));
  and and_8 (and_8_out, enR8, ~STORE);  // AND_Gate
  and and_9 (and_9_out, enR9, ~STORE);  // AND_Gate
  and and_10 (and_10_out, enR10, ~STORE);  // AND_Gate
  and and_11 (and_11_out, enR11, ~STORE);  // AND_Gate
  and and_12 (and_12_out, enR12, ~STORE);  // AND_Gate
  and and_13 (and_13_out, enR13, ~STORE);  // AND_Gate
  and and_14 (and_14_out, enR14, ~STORE);  // AND_Gate
  and and_15 (and_15_out, enR15, ~STORE);  // AND_Gate
  Register #(.width(16)) register_9 (.D(toR8), .en(and_8_out), .clk(Clock), .Q(R8), .clr(reset));
  Register #(.width(16)) register_10 (.D(toR9), .en(and_9_out), .clk(Clock), .Q(R9), .clr(reset));
  Register #(.width(16)) register_11 (.D(toR10), .en(and_10_out), .clk(Clock), .Q(R10), .clr(reset));
  Register #(.width(16)) register_12 (.D(toR11), .en(and_11_out), .clk(Clock), .Q(R11), .clr(reset));
  Register #(.width(16)) register_13 (.D(toR12), .en(and_12_out), .clk(Clock), .Q(Rg_2[15:0]), .clr(reset));
  Register #(.width(16)) register_14 (.D(toR13), .en(and_13_out), .clk(Clock), .Q(Rg_2[31:16]), .clr(reset));
  Register #(.width(16)) register_15 (.D(Ra_out), .en(and_14_out), .clk(Clock), .Q(Rg_2[47:32]), .clr(reset));
  Register #(.width(16)) register_16 (.D(toR15), .en(and_15_out), .clk(Clock), .Q(Rg_2[63:48]), .clr(reset));
  Multiplexer #(.select(4), .width(16)) multiplexer_2 (
    .in0(R0), .in1(Rg_1[15:0]), .in2(Rg_1[31:16]), .in3(Rg_1[47:32]), .in4(R4), .in5(R5), .in6(R6), .in7(R7),
    .in8(R8), .in9(R9), .in10(R10), .in11(R11), .in12(Rg_2[15:0]), .in13(Rg_2[31:16]), .in14(Rg_2[47:32]),
    .in15(Rg_2[63:48]), .out(Ra_out), .sel(Instruction[7:4]));
  Multiplexer #(.select(4), .width(16)) multiplexer_3 (
    .in0(R0), .in1(Rg_1[15:0]), .in2(Rg_1[31:16]), .in3(Rg_1[47:32]), .in4(R4), .in5(R5), .in6(R6), .in7(R7),
    .in8(R8), .in9(R9), .in10(R10), .in11(R11), .in12(Rg_2[15:0]), .in13(Rg_2[31:16]), .in14(Rg_2[47:32]),
    .in15(Rg_2[63:48]), .out(PC_out), .sel(Instruction[3:0]));
  Multiplexer #(.select(4), .width(16)) multiplexer_4 (
    .in0(R0), .in1(Rg_1[15:0]), .in2(Rg_1[31:16]), .in3(Rg_1[47:32]), .in4(R4), .in5(R5), .in6(R6), .in7(R7),
    .in8(R8), .in9(R9), .in10(R10), .in11(R11), .in12(Rg_2[15:0]), .in13(Rg_2[31:16]), .in14(Rg_2[47:32]),
    .in15(Rg_2[63:48]), .out(Rd_out), .sel(d));

  assign Rb_out = PC_out;

  // Other names for the same wires on the sheet: Clk = Clock; FP[15:0] = Ra_out; b[3:0] = Instruction[3:0];
  //   a[3:0] = Instruction[7:4]; op[3:0] = Instruction[15:12]; on_inst_two_c = ins_two_c; r = reset; Rd[15:0] = Rd_in;
  //   R1[15:0] = Rg_1[15:0]; R2[15:0] = Rg_1[31:16]; R3[15:0] = Rg_1[47:32]; R12[15:0] = Rg_2[15:0];
  //   R13[15:0] = Rg_2[31:16]; R14[15:0] = Rg_2[47:32]; R15[15:0] = Rg_2[63:48]; st = STORE

  // Notes on the sheet:
  //   On a CALL/RETURN:
  //   If storing, don't alter registers
  //   Want to put into Rb
  //   Old FP goes into Ra
  //   Ra goes into FP
  //   Getting correct enables
  //   Logic to swap a and d if the special instruction is present
  //   R0 fixed at 0
  //   Selecting what registers to write to
  //   R14 = FP (frame pointer)
  //   R15 = SP (stack pointer)
  //   for main circuit displaying purpose
  //   R11-R13 have special usage (function calls, branching, etc.)
endmodule

module HERA_Register (
  input  [15:0] D,
  input  Enable,
  input  Clock,
  output [15:0] Q
);

  wire clk;

  and and_1 (clk, Enable, Clock);
  D_Flip_Flop d_ff_1 (.D(D[0]), .clk(clk), .Q(Q[0]));  // open: Qn, preset, reset
  D_Flip_Flop d_ff_2 (.D(D[1]), .clk(clk), .Q(Q[1]));  // open: Qn, preset, reset
  D_Flip_Flop d_ff_3 (.D(D[2]), .clk(clk), .Q(Q[2]));  // open: Qn, preset, reset
  D_Flip_Flop d_ff_4 (.D(D[3]), .clk(clk), .Q(Q[3]));  // open: Qn, preset, reset
  D_Flip_Flop d_ff_5 (.D(D[4]), .clk(clk), .Q(Q[4]));  // open: Qn, preset, reset
  D_Flip_Flop d_ff_6 (.D(D[5]), .clk(clk), .Q(Q[5]));  // open: Qn, preset, reset
  D_Flip_Flop d_ff_7 (.D(D[6]), .clk(clk), .Q(Q[6]));  // open: Qn, preset, reset
  D_Flip_Flop d_ff_8 (.D(D[7]), .clk(clk), .Q(Q[7]));  // open: Qn, preset, reset
  D_Flip_Flop d_ff_9 (.D(D[8]), .clk(clk), .Q(Q[8]));  // open: Qn, preset, reset
  D_Flip_Flop d_ff_10 (.D(D[9]), .clk(clk), .Q(Q[9]));  // open: Qn, preset, reset
  D_Flip_Flop d_ff_11 (.D(D[10]), .clk(clk), .Q(Q[10]));  // open: Qn, preset, reset
  D_Flip_Flop d_ff_12 (.D(D[11]), .clk(clk), .Q(Q[11]));  // open: Qn, preset, reset
  D_Flip_Flop d_ff_13 (.D(D[12]), .clk(clk), .Q(Q[12]));  // open: Qn, preset, reset
  D_Flip_Flop d_ff_14 (.D(D[13]), .clk(clk), .Q(Q[13]));  // open: Qn, preset, reset
  D_Flip_Flop d_ff_15 (.D(D[14]), .clk(clk), .Q(Q[14]));  // open: Qn, preset, reset
  D_Flip_Flop d_ff_16 (.D(D[15]), .clk(clk), .Q(Q[15]));  // open: Qn, preset, reset

  // Notes on the sheet:
  //   Each bit in D gets sent to a D Flip-Flop
endmodule

module RegSelect (
  input  [15:0] Instruction,
  input  [15:0] Rd,
  input  [15:0] New_PC,
  input  [15:0] Old_FP,
  output [15:0] R1,
  output [15:0] out_6,
  output [15:0] out_7,
  output [15:0] out_8,
  output [15:0] out_9,
  output [15:0] out_10,
  output [15:0] out_11,
  output [15:0] out_12,
  output [15:0] out_13,
  output [15:0] out_14,
  output [15:0] out_15,
  output [15:0] out_16,
  output [15:0] out_17,
  output [15:0] out_18,
  output [15:0] out_19
);

  wire and_1_out, and_2_out, and_33_out, CaRt, one_or_zero;
  wire [1:0] and_3_out, and_5_out, and_7_out, and_9_out, and_11_out, and_13_out, and_15_out, and_17_out,
       and_19_out, and_21_out, and_23_out, and_25_out, and_27_out, and_29_out, and_31_out, and_35_out,
       and_36_out, and_37_out, and_38_out, and_39_out, and_40_out, and_41_out, and_42_out, and_43_out,
       and_44_out, and_45_out, and_46_out, and_47_out, and_48_out, and_49_out;

  and and_1 (and_1_out, ~Instruction[8], ~Instruction[9], ~Instruction[10], ~Instruction[11]);  // AND_Gate
  and and_2 (and_2_out, ~Instruction[12], Instruction[13], ~Instruction[14], ~Instruction[15]);  // AND_Gate
  and and_3 (and_3_out[0], Instruction[0], ~Instruction[1], ~Instruction[2], ~Instruction[3]);  // AND_Gate
  and and_4 (and_3_out[1], Instruction[4], ~Instruction[5], ~Instruction[6], ~Instruction[7]);  // AND_Gate
  and and_5 (and_5_out[0], ~Instruction[0], Instruction[1], ~Instruction[2], ~Instruction[3]);  // AND_Gate
  and and_6 (and_5_out[1], ~Instruction[4], Instruction[5], ~Instruction[6], ~Instruction[7]);  // AND_Gate
  and and_7 (and_7_out[0], Instruction[0], Instruction[1], ~Instruction[2], ~Instruction[3]);  // AND_Gate
  and and_8 (and_7_out[1], Instruction[4], Instruction[5], ~Instruction[6], ~Instruction[7]);  // AND_Gate
  and and_9 (and_9_out[0], ~Instruction[0], ~Instruction[1], Instruction[2], ~Instruction[3]);  // AND_Gate
  and and_10 (and_9_out[1], ~Instruction[4], ~Instruction[5], Instruction[6], ~Instruction[7]);  // AND_Gate
  and and_11 (and_11_out[0], Instruction[0], ~Instruction[1], Instruction[2], ~Instruction[3]);  // AND_Gate
  and and_12 (and_11_out[1], Instruction[4], ~Instruction[5], Instruction[6], ~Instruction[7]);  // AND_Gate
  and and_13 (and_13_out[0], ~Instruction[0], Instruction[1], Instruction[2], ~Instruction[3]);  // AND_Gate
  and and_14 (and_13_out[1], ~Instruction[4], Instruction[5], Instruction[6], ~Instruction[7]);  // AND_Gate
  and and_15 (and_15_out[0], Instruction[0], Instruction[1], Instruction[2], ~Instruction[3]);  // AND_Gate
  and and_16 (and_15_out[1], Instruction[4], Instruction[5], Instruction[6], ~Instruction[7]);  // AND_Gate
  and and_17 (and_17_out[0], ~Instruction[0], ~Instruction[1], ~Instruction[2], Instruction[3]);  // AND_Gate
  and and_18 (and_17_out[1], ~Instruction[4], ~Instruction[5], ~Instruction[6], Instruction[7]);  // AND_Gate
  and and_19 (and_19_out[0], Instruction[0], ~Instruction[1], ~Instruction[2], Instruction[3]);  // AND_Gate
  and and_20 (and_19_out[1], Instruction[4], ~Instruction[5], ~Instruction[6], Instruction[7]);  // AND_Gate
  and and_21 (and_21_out[0], ~Instruction[0], Instruction[1], ~Instruction[2], Instruction[3]);  // AND_Gate
  and and_22 (and_21_out[1], ~Instruction[4], Instruction[5], ~Instruction[6], Instruction[7]);  // AND_Gate
  and and_23 (and_23_out[0], Instruction[0], Instruction[1], ~Instruction[2], Instruction[3]);  // AND_Gate
  and and_24 (and_23_out[1], Instruction[4], Instruction[5], ~Instruction[6], Instruction[7]);  // AND_Gate
  and and_25 (and_25_out[0], ~Instruction[0], ~Instruction[1], Instruction[2], Instruction[3]);  // AND_Gate
  and and_26 (and_25_out[1], ~Instruction[4], ~Instruction[5], Instruction[6], Instruction[7]);  // AND_Gate
  and and_27 (and_27_out[0], Instruction[0], ~Instruction[1], Instruction[2], Instruction[3]);  // AND_Gate
  and and_28 (and_27_out[1], Instruction[4], ~Instruction[5], Instruction[6], Instruction[7]);  // AND_Gate
  and and_29 (and_29_out[0], ~Instruction[0], Instruction[1], Instruction[2], Instruction[3]);  // AND_Gate
  and and_30 (and_29_out[1], ~Instruction[4], Instruction[5], Instruction[6], Instruction[7]);  // AND_Gate
  and and_31 (and_31_out[0], Instruction[0], Instruction[1], Instruction[2], Instruction[3]);
  and and_32 (and_31_out[1], Instruction[4], Instruction[5], Instruction[6], Instruction[7]);
  and and_33 (and_33_out, Instruction[8], ~Instruction[9], ~Instruction[10], ~Instruction[11]);  // AND_Gate
  and and_34 (CaRt, one_or_zero, and_2_out);
  assign and_35_out = {2{CaRt}} & and_3_out;  // AND_Gate and_35, 2 bits wide
  assign and_36_out = {2{CaRt}} & and_5_out;  // AND_Gate and_36, 2 bits wide
  assign and_37_out = {2{CaRt}} & and_7_out;  // AND_Gate and_37, 2 bits wide
  assign and_38_out = {2{CaRt}} & and_9_out;  // AND_Gate and_38, 2 bits wide
  assign and_39_out = {2{CaRt}} & and_11_out;  // AND_Gate and_39, 2 bits wide
  assign and_40_out = {2{CaRt}} & and_13_out;  // AND_Gate and_40, 2 bits wide
  assign and_41_out = {2{CaRt}} & and_15_out;  // AND_Gate and_41, 2 bits wide
  assign and_42_out = {2{CaRt}} & and_17_out;  // AND_Gate and_42, 2 bits wide
  assign and_43_out = {2{CaRt}} & and_19_out;  // AND_Gate and_43, 2 bits wide
  assign and_44_out = {2{CaRt}} & and_21_out;  // AND_Gate and_44, 2 bits wide
  assign and_45_out = {2{CaRt}} & and_23_out;  // AND_Gate and_45, 2 bits wide
  assign and_46_out = {2{CaRt}} & and_25_out;  // AND_Gate and_46, 2 bits wide
  assign and_47_out = {2{CaRt}} & and_27_out;  // AND_Gate and_47, 2 bits wide
  assign and_48_out = {2{CaRt}} & and_29_out;  // AND_Gate and_48, 2 bits wide
  assign and_49_out = {2{CaRt}} & and_31_out;  // AND_Gate and_49, 2 bits wide
  Multiplexer #(.select(2), .width(16)) multiplexer_1 (
    .in0(Rd), .in1(New_PC), .in2(Old_FP), .out(R1), .sel(and_35_out));  // open: in3
  Multiplexer #(.select(2), .width(16)) multiplexer_2 (
    .in0(Rd), .in1(New_PC), .in2(Old_FP), .out(out_6), .sel(and_36_out));  // open: in3
  Multiplexer #(.select(2), .width(16)) multiplexer_3 (
    .in0(Rd), .in1(New_PC), .in2(Old_FP), .out(out_7), .sel(and_37_out));  // open: in3
  Multiplexer #(.select(2), .width(16)) multiplexer_4 (
    .in0(Rd), .in1(New_PC), .in2(Old_FP), .out(out_8), .sel(and_38_out));  // open: in3
  Multiplexer #(.select(2), .width(16)) multiplexer_5 (
    .in0(Rd), .in1(New_PC), .in2(Old_FP), .out(out_9), .sel(and_39_out));  // open: in3
  Multiplexer #(.select(2), .width(16)) multiplexer_6 (
    .in0(Rd), .in1(New_PC), .in2(Old_FP), .out(out_10), .sel(and_40_out));  // open: in3
  Multiplexer #(.select(2), .width(16)) multiplexer_7 (
    .in0(Rd), .in1(New_PC), .in2(Old_FP), .out(out_11), .sel(and_41_out));  // open: in3
  Multiplexer #(.select(2), .width(16)) multiplexer_8 (
    .in0(Rd), .in1(New_PC), .in2(Old_FP), .out(out_12), .sel(and_42_out));  // open: in3
  Multiplexer #(.select(2), .width(16)) multiplexer_9 (
    .in0(Rd), .in1(New_PC), .in2(Old_FP), .out(out_13), .sel(and_43_out));  // open: in3
  Multiplexer #(.select(2), .width(16)) multiplexer_10 (
    .in0(Rd), .in1(New_PC), .in2(Old_FP), .out(out_14), .sel(and_44_out));  // open: in3
  Multiplexer #(.select(2), .width(16)) multiplexer_11 (
    .in0(Rd), .in1(New_PC), .in2(Old_FP), .out(out_15), .sel(and_45_out));  // open: in3
  Multiplexer #(.select(2), .width(16)) multiplexer_12 (
    .in0(Rd), .in1(New_PC), .in2(Old_FP), .out(out_16), .sel(and_46_out));  // open: in3
  Multiplexer #(.select(2), .width(16)) multiplexer_13 (
    .in0(Rd), .in1(New_PC), .in2(Old_FP), .out(out_17), .sel(and_47_out));  // open: in3
  Multiplexer #(.select(2), .width(16)) multiplexer_14 (
    .in0(Rd), .in1(New_PC), .in2(Old_FP), .out(out_18), .sel(and_48_out));  // open: in3
  Multiplexer #(.select(2), .width(16)) multiplexer_15 (
    .in0(Rd), .in1(New_PC), .in2(Old_FP), .out(out_19), .sel(and_49_out));  // open: in3
  or or_1 (one_or_zero, and_33_out, and_1_out);

  // Other names for the same wires on the sheet: FP[15:0] = Old_FP; b[3:0] = Instruction[3:0];
  //   a[3:0] = Instruction[7:4]; d[3:0] = Instruction[11:8]; PC[15:0] = New_PC

  // Notes on the sheet:
  //   If CALL/RETURN
  //   Checking if d has either a 1 and then all 0's or all 0's in order for the special instruction to work
  //   This then gets plugged in with the opcode instruction to ensure both are working i.e there is a 2 in the opcode as well as what was stated above
endmodule

module RegEnable (
  input  [3:0] opcode,
  input  [3:0] Rd,
  input  [3:0] Ra,
  input  [3:0] Rb,
  output R1,
  output R2,
  output R3,
  output R4,
  output R5,
  output R6,
  output R7,
  output R8,
  output R9,
  output R10,
  output R11,
  output R12,
  output R13,
  output R14,
  output R15
);

  wire and_2_out, and_3_out, and_4_out, and_5_out, and_6_out, and_7_out, and_8_out, and_9_out, and_10_out,
       and_11_out, and_12_out, and_13_out, and_14_out, and_15_out, and_16_out, and_17_out, and_18_out,
       and_19_out, and_20_out, and_21_out, and_22_out, and_23_out, and_24_out, and_25_out, and_26_out,
       and_27_out, and_28_out, and_29_out, and_30_out, and_31_out, and_32_out, and_33_out, and_34_out,
       and_35_out, and_36_out, and_37_out, and_38_out, and_39_out, and_40_out, and_41_out, and_42_out,
       and_43_out, and_44_out, and_45_out, and_46_out, and_47_out, and_48_out, and_49_out, and_50_out,
       and_51_out, and_52_out, and_53_out, and_54_out, and_55_out, and_56_out, and_57_out, and_58_out,
       and_59_out, and_60_out, and_61_out, and_62_out, and_63_out, and_64_out, and_65_out, and_66_out,
       and_67_out, and_68_out, and_69_out, and_70_out, and_71_out, and_72_out, and_73_out, and_74_out,
       and_75_out, and_76_out, and_77_out, and_78_out, and_79_out, and_80_out, and_81_out, and_82_out,
       and_83_out, and_84_out, and_85_out, and_86_out, and_87_out, and_88_out, and_89_out, and_90_out,
       and_91_out, and_92_out, and_106_out, comparator_1_eq, comparator_2_eq, is_branch, or_1_out, or_2_out,
       or_3_out, or_4_out, or_5_out, or_6_out, or_7_out, or_8_out, or_9_out, or_10_out, or_11_out, or_12_out,
       or_13_out, or_14_out, or_15_out;

  and and_1 (is_branch, ~opcode[1], ~opcode[2], ~opcode[3]);  // AND_Gate
  and and_2 (and_2_out, ~opcode[0], opcode[1], ~opcode[2], ~opcode[3]);  // AND_Gate
  and and_3 (and_3_out, Rd[0], ~Rd[1], ~Rd[2], ~Rd[3]);  // AND_Gate
  and and_4 (and_4_out, Ra[0], ~Ra[1], ~Ra[2], ~Ra[3]);  // AND_Gate
  and and_5 (and_5_out, Rb[0], ~Rb[1], ~Rb[2], ~Rb[3]);  // AND_Gate
  and and_6 (and_6_out, ~Rd[0], Rd[1], ~Rd[2], ~Rd[3]);  // AND_Gate
  and and_7 (and_7_out, ~Ra[0], Ra[1], ~Ra[2], ~Ra[3]);  // AND_Gate
  and and_8 (and_8_out, ~Rb[0], Rb[1], ~Rb[2], ~Rb[3]);  // AND_Gate
  and and_9 (and_9_out, Rd[0], Rd[1], ~Rd[2], ~Rd[3]);  // AND_Gate
  and and_10 (and_10_out, Ra[0], Ra[1], ~Ra[2], ~Ra[3]);  // AND_Gate
  and and_11 (and_11_out, Rb[0], Rb[1], ~Rb[2], ~Rb[3]);  // AND_Gate
  and and_12 (and_12_out, ~Rd[0], ~Rd[1], Rd[2], ~Rd[3]);  // AND_Gate
  and and_13 (and_13_out, ~Ra[0], ~Ra[1], Ra[2], ~Ra[3]);  // AND_Gate
  and and_14 (and_14_out, ~Rb[0], ~Rb[1], Rb[2], ~Rb[3]);  // AND_Gate
  and and_15 (and_15_out, Rd[0], ~Rd[1], Rd[2], ~Rd[3]);  // AND_Gate
  and and_16 (and_16_out, Ra[0], ~Ra[1], Ra[2], ~Ra[3]);  // AND_Gate
  and and_17 (and_17_out, Rb[0], ~Rb[1], Rb[2], ~Rb[3]);  // AND_Gate
  and and_18 (and_18_out, ~Rd[0], Rd[1], Rd[2], ~Rd[3]);  // AND_Gate
  and and_19 (and_19_out, ~Ra[0], Ra[1], Ra[2], ~Ra[3]);  // AND_Gate
  and and_20 (and_20_out, ~Rb[0], Rb[1], Rb[2], ~Rb[3]);  // AND_Gate
  and and_21 (and_21_out, Rd[0], Rd[1], Rd[2], ~Rd[3]);  // AND_Gate
  and and_22 (and_22_out, Ra[0], Ra[1], Ra[2], ~Ra[3]);  // AND_Gate
  and and_23 (and_23_out, Rb[0], Rb[1], Rb[2], ~Rb[3]);  // AND_Gate
  and and_24 (and_24_out, ~Rd[0], ~Rd[1], ~Rd[2], Rd[3]);  // AND_Gate
  and and_25 (and_25_out, ~Ra[0], ~Ra[1], ~Ra[2], Ra[3]);  // AND_Gate
  and and_26 (and_26_out, ~Rb[0], ~Rb[1], ~Rb[2], Rb[3]);  // AND_Gate
  and and_27 (and_27_out, Rd[0], ~Rd[1], ~Rd[2], Rd[3]);  // AND_Gate
  and and_28 (and_28_out, Ra[0], ~Ra[1], ~Ra[2], Ra[3]);  // AND_Gate
  and and_29 (and_29_out, Rb[0], ~Rb[1], ~Rb[2], Rb[3]);  // AND_Gate
  and and_30 (and_30_out, ~Rd[0], Rd[1], ~Rd[2], Rd[3]);  // AND_Gate
  and and_31 (and_31_out, ~Ra[0], Ra[1], ~Ra[2], Ra[3]);  // AND_Gate
  and and_32 (and_32_out, ~Rb[0], Rb[1], ~Rb[2], Rb[3]);  // AND_Gate
  and and_33 (and_33_out, Rd[0], Rd[1], ~Rd[2], Rd[3]);  // AND_Gate
  and and_34 (and_34_out, Ra[0], Ra[1], ~Ra[2], Ra[3]);  // AND_Gate
  and and_35 (and_35_out, Rb[0], Rb[1], ~Rb[2], Rb[3]);  // AND_Gate
  and and_36 (and_36_out, ~Rd[0], ~Rd[1], Rd[2], Rd[3]);  // AND_Gate
  and and_37 (and_37_out, ~Ra[0], ~Ra[1], Ra[2], Ra[3]);  // AND_Gate
  and and_38 (and_38_out, ~Rb[0], ~Rb[1], Rb[2], Rb[3]);  // AND_Gate
  and and_39 (and_39_out, Rd[0], ~Rd[1], Rd[2], Rd[3]);  // AND_Gate
  and and_40 (and_40_out, Ra[0], ~Ra[1], Ra[2], Ra[3]);  // AND_Gate
  and and_41 (and_41_out, Rb[0], ~Rb[1], Rb[2], Rb[3]);  // AND_Gate
  and and_42 (and_42_out, ~Rd[0], Rd[1], Rd[2], Rd[3]);  // AND_Gate
  and and_43 (and_43_out, ~Ra[0], Ra[1], Ra[2], Ra[3]);  // AND_Gate
  and and_44 (and_44_out, ~Rb[0], Rb[1], Rb[2], Rb[3]);  // AND_Gate
  and and_45 (and_45_out, Rd[0], Rd[1], Rd[2], Rd[3]);
  and and_46 (and_46_out, Ra[0], Ra[1], Ra[2], Ra[3]);
  and and_47 (and_47_out, Rb[0], Rb[1], Rb[2], Rb[3]);
  and and_48 (and_48_out, ~and_2_out, and_3_out);  // AND_Gate
  and and_49 (and_49_out, and_2_out, and_4_out);
  and and_50 (and_50_out, and_2_out, and_5_out);
  and and_51 (and_51_out, ~and_2_out, and_6_out);  // AND_Gate
  and and_52 (and_52_out, and_2_out, and_7_out);
  and and_53 (and_53_out, and_2_out, and_8_out);
  and and_54 (and_54_out, ~and_2_out, and_9_out);  // AND_Gate
  and and_55 (and_55_out, and_2_out, and_10_out);
  and and_56 (and_56_out, and_2_out, and_11_out);
  and and_57 (and_57_out, ~and_2_out, and_12_out);  // AND_Gate
  and and_58 (and_58_out, and_2_out, and_13_out);
  and and_59 (and_59_out, and_2_out, and_14_out);
  and and_60 (and_60_out, ~and_2_out, and_15_out);  // AND_Gate
  and and_61 (and_61_out, and_2_out, and_16_out);
  and and_62 (and_62_out, and_2_out, and_17_out);
  and and_63 (and_63_out, ~and_2_out, and_18_out);  // AND_Gate
  and and_64 (and_64_out, and_19_out, and_2_out);
  and and_65 (and_65_out, and_2_out, and_20_out);
  and and_66 (and_66_out, ~and_2_out, and_21_out);  // AND_Gate
  and and_67 (and_67_out, and_2_out, and_22_out);
  and and_68 (and_68_out, and_2_out, and_23_out);
  and and_69 (and_69_out, ~and_2_out, and_24_out);  // AND_Gate
  and and_70 (and_70_out, and_25_out, and_2_out);
  and and_71 (and_71_out, and_2_out, and_26_out);
  and and_72 (and_72_out, ~and_2_out, and_27_out);  // AND_Gate
  and and_73 (and_73_out, and_28_out, and_2_out);
  and and_74 (and_74_out, and_2_out, and_29_out);
  and and_75 (and_75_out, ~and_2_out, and_30_out);  // AND_Gate
  and and_76 (and_76_out, and_2_out, and_31_out);
  and and_77 (and_77_out, and_2_out, and_32_out);
  and and_78 (and_78_out, ~and_2_out, and_33_out);  // AND_Gate
  and and_79 (and_79_out, and_34_out, and_2_out);
  and and_80 (and_80_out, and_2_out, and_35_out);
  and and_81 (and_81_out, ~and_2_out, and_36_out);  // AND_Gate
  and and_82 (and_82_out, and_2_out, and_37_out);
  and and_83 (and_83_out, and_2_out, and_38_out);
  and and_84 (and_84_out, ~and_2_out, and_39_out);  // AND_Gate
  and and_85 (and_85_out, and_2_out, and_40_out);
  and and_86 (and_86_out, and_2_out, and_41_out);
  and and_87 (and_87_out, ~and_2_out, and_42_out);  // AND_Gate
  and and_88 (and_88_out, and_2_out, and_43_out);
  and and_89 (and_89_out, and_2_out, and_44_out);
  and and_90 (and_90_out, ~and_2_out, and_45_out);  // AND_Gate
  and and_91 (and_91_out, and_2_out, and_46_out);
  and and_92 (and_92_out, and_2_out, and_47_out);
  or or_1 (or_1_out, and_48_out, and_49_out, and_50_out);
  or or_2 (or_2_out, and_54_out, and_55_out, and_56_out);
  or or_3 (or_3_out, and_57_out, and_58_out, and_59_out);
  or or_4 (or_4_out, and_60_out, and_61_out, and_62_out);
  or or_5 (or_5_out, and_72_out, and_73_out, and_74_out);
  or or_6 (or_6_out, and_75_out, and_76_out, and_77_out);
  or or_7 (or_7_out, and_78_out, and_79_out, and_80_out);
  or or_8 (or_8_out, and_51_out, and_52_out, and_53_out);
  or or_9 (or_9_out, and_63_out, and_64_out, and_65_out);
  or or_10 (or_10_out, and_66_out, and_67_out, and_68_out);
  or or_11 (or_11_out, and_69_out, and_70_out, and_71_out);
  or or_12 (or_12_out, and_81_out, and_82_out, and_83_out);
  or or_13 (or_13_out, and_84_out, and_85_out, and_86_out);
  or or_14 (or_14_out, and_87_out, and_88_out, and_89_out);
  or or_15 (or_15_out, and_90_out, and_91_out, and_92_out);
  and and_93 (R1, or_1_out, ~is_branch);  // AND_Gate
  and and_94 (R2, or_8_out, ~is_branch);  // AND_Gate
  and and_95 (R3, or_2_out, ~is_branch);  // AND_Gate
  and and_96 (R4, or_3_out, ~is_branch);  // AND_Gate
  and and_97 (R5, or_4_out, ~is_branch);  // AND_Gate
  and and_98 (R6, or_9_out, ~is_branch);  // AND_Gate
  and and_99 (R7, or_10_out, ~is_branch);  // AND_Gate
  and and_100 (R8, or_11_out, ~is_branch);  // AND_Gate
  and and_101 (R9, or_5_out, ~is_branch);  // AND_Gate
  and and_102 (R10, or_6_out, ~is_branch);  // AND_Gate
  and and_103 (R11, or_7_out, ~is_branch);  // AND_Gate
  and and_104 (R12, or_12_out, ~is_branch);  // AND_Gate
  and and_105 (R13, or_13_out, ~is_branch);  // AND_Gate
  and and_106 (and_106_out, or_14_out, ~is_branch);  // AND_Gate
  and and_107 (R15, or_15_out, ~is_branch);  // AND_Gate
  Comparator #(.width(16)) comparator_1 (.a({opcode, Rd, Ra, Rb}), .b(16'h20cd), .eq(comparator_1_eq));  // open: gt, lt
  Comparator #(.width(16)) comparator_2 (.a({opcode, Rd, Ra, Rb}), .b(16'h21cd), .eq(comparator_2_eq));  // open: gt, lt
  or or_16 (R14, and_106_out, comparator_1_eq, comparator_2_eq);

  // Other names for the same wires on the sheet: instruction[15:0] = {opcode, Rd, Ra, Rb}
endmodule
